# Fritzing sketch MC1_schematic (saved by Fritzing 0.9.2b)
breadboards: 1

parts:
  Arduino = Arduino Uno (Rev3)
  U1 = TLC5916 [package="DIP16 [THT]"]
  U2 = TLC5916 [package="DIP16 [THT]"]
  U3 = TLC5916 [package="DIP16 [THT]"]
  U4 = TLC5916 [package="DIP16 [THT]"]
  U5 = TLC5916 [package="DIP16 [THT]"]
  U6 = TLC5916 [package="DIP16 [THT]"]
  LED1 = RGB LED (com. anode, rbg) [package="5 mm [THT]"]
  LED2 = RGB LED (com. anode, rbg) [package="5 mm [THT]"]
  LED3 = RGB LED (com. anode, rbg) [package="5 mm [THT]"]
  LED4 = RGB LED (com. anode, rbg) [package="5 mm [THT]"]
  LED7 = RGB LED (com. anode, rbg) [package="5 mm [THT]"]
  LED6 = RGB LED (com. anode, rbg) [package="5 mm [THT]"]
  LED8 = RGB LED (com. anode, rbg) [package="5 mm [THT]"]
  LED9 = RGB LED (com. anode, rbg) [package="5 mm [THT]"]
  LED16 = RGB LED (com. anode, rbg) [package="5 mm [THT]"]
  LED11 = RGB LED (com. anode, rbg) [package="5 mm [THT]"]
  LED15 = RGB LED (com. anode, rbg) [package="5 mm [THT]"]
  LED12 = RGB LED (com. anode, rbg) [package="5 mm [THT]"]
  LED14 = RGB LED (com. anode, rbg) [package="5 mm [THT]"]
  LED13 = RGB LED (com. anode, rbg) [package="5 mm [THT]"]
  LED10 = RGB LED (com. anode, rbg) [package="5 mm [THT]"]
  R1 = Resistor [tolerance=±5% resistance=1k package=THT]
  R2 = Resistor [tolerance=±5% resistance=1k package=THT]
  R3 = Resistor [tolerance=±5% resistance=1k package=THT]
  R4 = Resistor [tolerance=±5% resistance=1k package=THT]
  R5 = Resistor [tolerance=±5% resistance=1k package=THT]
  R6 = Resistor [tolerance=±5% resistance=1k package=THT]
  LED5 = RGB LED (com. anode, rbg) [package="5 mm [THT]"]
  U7 = 74HC165 [part_number=SN74LS165 package="DIP16 [THT]"]
  U8 = 74HC165 [part_number=SN74LS165 package="DIP16 [THT]"]
  S1 = Pushbutton [package=THT]
  S2 = Pushbutton [package=THT]
  S3 = Pushbutton [package=THT]
  S4 = Pushbutton [package=THT]
  S5 = Pushbutton [package=THT]
  S6 = Pushbutton [package=THT]
  S7 = Pushbutton [package=THT]
  S8 = Pushbutton [package=THT]
  S9 = Pushbutton [package=THT]
  S10 = Pushbutton [package=THT]
  S11 = Pushbutton [package=THT]
  S12 = Pushbutton [package=THT]
  S13 = Pushbutton [package=THT]
  S14 = Pushbutton [package=THT]
  S15 = Pushbutton [package=THT]
  S16 = Pushbutton [package=THT]
  LCD1 = LCD screen
  U9 = 74HC595 [package="DIP16 [THT]"]
  R7 = Trimmer Potentiometer [maximum_resistance=10kΩ package=THT]
  Q1 = TRANSISTOR_NPN [package=sot223]
  Q1_2 = TRANSISTOR_NPN [package=sot23]  # not connected
  Q1_3 = TRANSISTOR_NPN [package=sot89]  # not connected
  Q1_4 = TRANSISTOR_NPN [part_number=BC550 package=sot23]  # not connected
  U10 = Optocoupler [package=THT]
  D1 = Rectifier Diode [part_number=1N4001 package="300 mil [THT]"]
  R8 = Resistor [tolerance=±5% resistance=220 package=THT]
  R9 = Resistor [tolerance=±5% resistance=1M package=THT]
  R10 = Resistor [tolerance=±5% resistance=3.3k package=THT]
  MIDI_IN = DIN-5 jack (MIDI) [package=THT]
  MIDI_OUT = DIN-5 jack (MIDI) [package=THT]
  R11 = Resistor [tolerance=±5% resistance=220 package=THT]
  R12 = Resistor [tolerance=±5% resistance=220 package=THT]
  U11 = RJ45 Jack [package=rj45-8]
  9V_Barrel_Jack = Power Jack [package=power_jack_pth_lock]
  MIDI_IN1 = DIN-5 jack (MIDI) [package=THT]
  MIDI_OUT1 = DIN-5 jack (MIDI) [package=THT]
  U13 = RJ45 Jack [package=rj45-8]
  9V_Barrel_Jack1 = Power Jack [package=power_jack_pth_lock]
  EXP1 = AMPHENOL - ACJS-MHDR [package=ACJS-MHDR]
  EXP2 = AMPHENOL - ACJS-MHDR [package=ACJS-MHDR]
  EXP3 = AMPHENOL - ACJS-MHDR [package=ACJS-MHDR]
  EXP4 = AMPHENOL - ACJS-MHDR [package=ACJS-MHDR]
  EXP5 = AMPHENOL - ACJS-MHDR [package=ACJS-MHDR]
  EXP6 = AMPHENOL - ACJS-MHDR [package=ACJS-MHDR]
  Power_Switch = Tilt Switch [package=THT]
  C1 = Electrolytic Capacitor [capacitance=0.1mF package="100 mil [THT, electrolytic]"]

nets:
  N1: Arduino.A0, EXP1.Ring_(5)
  N2: Arduino.A1, EXP2.Ring_(5)
  N3: Arduino.A2, EXP3.Ring_(5)
  N4: Arduino.A3, EXP4.Ring_(5)
  N5: Arduino.A4/SDA, EXP5.Ring_(5)
  N6: Arduino.A5/SCL, EXP6.Ring_(5)
  N7: Arduino.D8, U9.ST_CP
  N8: Arduino.D9_PWM, U9.SH_CP
  N9: Arduino.D10_PWM/SS, U1.LE(ED1), U2.LE(ED1), U3.LE(ED1), U4.LE(ED1), U5.LE(ED1), U6.LE(ED1)
  N10: Arduino.D11_PWM/MOSI, U1.SDI
  N11: Arduino.D13/SCK, U1.CLK, U2.CLK, U3.CLK, U4.CLK, U5.CLK, U6.CLK
  N12: Arduino.D0/RX, U10.Pin_5, R10.Pin_0
  N13: Arduino.D1/TX, R12.Pin_1
  N14: Arduino.D3_PWM, U7.Q1
  N15: Arduino.D4, U7.Q0
  N16: Arduino.D5_PWM, U7.Q7'
  N17: Arduino.D6_PWM, U7.Q2
  N18: Arduino.D7, U9.DS
  5V: Arduino.5V, U1.VDD, U2.VDD, U3.VDD, U4.VDD, U5.VDD, U6.VDD, LED1.common_anode, LED2.common_anode, LED3.common_anode, LED4.common_anode, LED7.common_anode, LED6.common_anode, LED8.common_anode, LED9.common_anode, LED16.common_anode, LED11.common_anode, LED15.common_anode, LED12.common_anode, LED14.common_anode, LED13.common_anode, LED10.common_anode, LED5.common_anode, S1.leg1, S2.leg1, S3.leg1, S4.leg1, S5.leg0, S6.leg0, S7.leg0, S8.leg0, S9.leg1, S10.leg1, S11.leg1, S12.leg1, S13.leg0, S14.leg0, S15.leg0, S16.leg0, LCD1.VDD, LCD1.LED+, U9.MR, U9.VCC, R7.leg2, R10.Pin_1, R11.Pin_1, EXP1.Tip_(6), EXP2.Tip_(6), EXP3.Tip_(6), EXP4.Tip_(6), EXP5.Tip_(6), EXP6.Tip_(6), C1.+
  GND: Arduino.GND, U1.GND, U1.OE(ED2), U2.GND, U2.OE(ED2), U3.GND, U3.OE(ED2), U4.GND, U4.OE(ED2), U5.GND, U5.OE(ED2), U6.GND, U6.OE(ED2), R1.Pin_1, R2.Pin_1, R3.Pin_1, R4.Pin_1, R5.Pin_1, R6.Pin_1, U7.GND, U8.GND, LCD1.VSS, LCD1.R/W, U9.OE, R7.leg1, Q1.E, U10.Pin_4, R9.Pin_1, MIDI_OUT.2, U11.1, U11.3, 9V_Barrel_Jack.PWR, U13.1, 9V_Barrel_Jack1.PWR, EXP1.Sleeve_(4), EXP2.Sleeve_(4), EXP3.Sleeve_(4), EXP4.Sleeve_(4), EXP5.Sleeve_(4), EXP6.Sleeve_(4), C1.-
  N19: Arduino.VIN, Power_Switch.Pin_2
  N20: U1.OUT0, LED1.red_cathode
  N21: U1.OUT1, LED1.blue_cathode
  N22: U1.OUT2, LED1.green_cathode
  N23: U1.OUT3, LED2.red_cathode
  N24: U1.OUT4, LED2.blue_cathode
  N25: U1.OUT5, LED2.green_cathode
  N26: U1.OUT6, LED3.red_cathode
  N27: U1.OUT7, LED3.blue_cathode
  N28: U1.SDO, U2.SDI
  N29: U1.R-EXT, R1.Pin_0
  N30: U2.OUT0, LED3.green_cathode
  N31: U2.OUT1, LED4.red_cathode
  N32: U2.OUT2, LED4.blue_cathode
  N33: U2.OUT3, LED4.green_cathode
  N34: U2.OUT4, LED5.red_cathode
  N35: U2.OUT5, LED5.blue_cathode
  N36: U2.OUT6, LED5.green_cathode
  N37: U2.OUT7, LED6.red_cathode
  N38: U2.SDO, U3.SDI
  N39: U2.R-EXT, R2.Pin_0
  N40: U3.OUT0, LED6.blue_cathode
  N41: U3.OUT1, LED6.green_cathode
  N42: U3.OUT2, LED7.red_cathode
  N43: U3.OUT3, LED7.blue_cathode
  N44: U3.OUT4, LED7.green_cathode
  N45: U3.OUT5, LED8.red_cathode
  N46: U3.OUT6, LED8.blue_cathode
  N47: U3.OUT7, LED8.green_cathode
  N48: U3.SDO, U4.SDI
  N49: U3.R-EXT, R3.Pin_0
  N50: U4.OUT0, LED9.red_cathode
  N51: U4.OUT1, LED9.blue_cathode
  N52: U4.OUT2, LED9.green_cathode
  N53: U4.OUT3, LED10.red_cathode
  N54: U4.OUT4, LED10.blue_cathode
  N55: U4.OUT5, LED10.green_cathode
  N56: U4.OUT6, LED11.red_cathode
  N57: U4.OUT7, LED11.blue_cathode
  N58: U4.SDO, U5.SDI
  N59: U4.R-EXT, R4.Pin_0
  N60: U5.OUT0, LED11.green_cathode
  N61: U5.OUT1, LED12.red_cathode
  N62: U5.OUT2, LED12.blue_cathode
  N63: U5.OUT3, LED12.green_cathode
  N64: U5.OUT4, LED13.red_cathode
  N65: U5.OUT5, LED13.blue_cathode
  N66: U5.OUT6, LED13.green_cathode
  N67: U5.OUT7, LED14.red_cathode
  N68: U5.SDO, U6.SDI
  N69: U5.R-EXT, R5.Pin_0
  N70: U6.OUT0, LED14.blue_cathode
  N71: U6.OUT1, LED14.green_cathode
  N72: U6.OUT2, LED15.red_cathode
  N73: U6.OUT3, LED15.blue_cathode
  N74: U6.OUT4, LED15.green_cathode
  N75: U6.OUT5, LED16.red_cathode
  N76: U6.OUT6, LED16.blue_cathode
  N77: U6.OUT7, LED16.green_cathode
  N78: U6.R-EXT, R6.Pin_0
  N79: U7.Q3, S13.leg1
  N80: U7.Q4, S14.leg1
  N81: U7.Q5, S15.leg1
  N82: U7.Q6, S16.leg1
  N83: U7.MR, U8.Q7'
  N84: U7.SH_CP, S9.leg0
  N85: U7.ST_CP, S10.leg0
  N86: U7.OE, S11.leg0
  N87: U7.DS, S12.leg0
  N88: U8.Q3, S5.leg1
  N89: U8.Q4, S6.leg1
  N90: U8.Q5, S7.leg1
  N91: U8.Q6, S8.leg1
  N92: U8.SH_CP, S1.leg0
  N93: U8.ST_CP, S2.leg0
  N94: U8.OE, S3.leg0
  N95: U8.DS, S4.leg0
  N96: LCD1.V0, R7.wiper
  N97: LCD1.RS, U9.Q7
  N98: LCD1.E, U9.Q0
  N99: LCD1.DB4, U9.Q4
  N100: LCD1.DB5, U9.Q3
  N101: LCD1.DB6, U9.Q2
  N102: LCD1.DB7, U9.Q1
  N103: LCD1.LED-, Q1.C
  N104: U9.Q6, Q1.B
  N105: U10.Pin_1, D1.cathode, R8.Pin_1
  N106: U10.Pin_2, D1.anode, MIDI_IN.5, U11.7
  N107: U10.Pin_6, R9.Pin_0
  N108: R8.Pin_0, MIDI_IN.4, U11.6
  N109: MIDI_OUT.5, R12.Pin_0, U11.5
  N110: MIDI_OUT.4, R11.Pin_0, U11.4
  N111: U11.2, 9V_Barrel_Jack.GND, Power_Switch.Pin_1
  N112: MIDI_IN1.5, U13.7
  N113: MIDI_IN1.4, U13.6
  N114: MIDI_OUT1.5, U13.5
  N115: MIDI_OUT1.2, U13.3
  N116: MIDI_OUT1.4, U13.4
  9V: U13.2, 9V_Barrel_Jack1.GND

notes:
  MIDI to RJ45 breakout box
  Switches 14, 15 and 16 are just TS jacks with tip wired to +5V and sleeve to appropriate 165N pin

custom parts:
  TLC5916: 8-bit led driver shift register
  74HC165: 8-bit parallel-load shift registers
